// Logisim project sem.circ as structural Verilog: 6 circuits, main circuit main
module main (
  input  RESET,
  output [5:0] out_2
);

  wire CLK_out, Decodificador_lav, Decodificador_lrp, Decodificador_lrv, Decodificador_lvp,
       Decodificador_lvv, maquina_de_estados_load, maquina_de_estados_s0, maquina_de_estados_s1,
       maquina_de_estados_se, maquina_de_estados_ts, mem_SP_sp_prime, mem_ZERO_zero_2, Solicitar_Paso_out,
       Tiempo_zero;
  wire [2:0] controlled_buffer_2_out, controlled_buffer_4_out, Tiempo_lsb_bot, Tiempo_msb_bot;
  wire [3:0] controlled_buffer_1_out, controlled_buffer_3_out, Tiempo_lsb_top, Tiempo_msb_top;

  Clock CLK (.out(CLK_out));
  Button Solicitar_Paso (.out(Solicitar_Paso_out));
  SP mem_SP (.CLK(CLK_out), .SP(Solicitar_Paso_out), .RES(RESET), .LVP(Decodificador_lvp), .SP_prime(mem_SP_sp_prime));
  Maquina_de_Estados maquina_de_estados (
    .CLK(CLK_out), .ZERO(mem_ZERO_zero_2), .SP_prime(mem_SP_sp_prime), .RES(RESET),
    .S1(maquina_de_estados_s1), .S0(maquina_de_estados_s0), .SE(maquina_de_estados_se),
    .LOAD(maquina_de_estados_load), .TS(maquina_de_estados_ts));
  ZERO mem_ZERO (
    .CLK(CLK_out), .ZERO(Tiempo_zero), .LOAD(maquina_de_estados_load), .RES(RESET), .ZERO_2(mem_ZERO_zero_2));
  Decodificador_de_Salidas Decodificador (
    .S1(maquina_de_estados_s1), .S0(maquina_de_estados_s0), .LRV(Decodificador_lrv), .LAV(Decodificador_lav),
    .LVV(Decodificador_lvv), .LRP(Decodificador_lrp), .LVP(Decodificador_lvp));
  assign controlled_buffer_1_out = maquina_de_estados_se ? Tiempo_msb_top : 4'bz;  // Controlled_Buffer controlled_buffer_1
  Tiempo Tiempo (
    .EN(1'b1), .CLK(CLK_out), .LOAD(maquina_de_estados_load), .TS(maquina_de_estados_ts), .num(out_2),
    .ZERO(Tiempo_zero), .LSB_top(Tiempo_lsb_top), .MSB_top(Tiempo_msb_top), .MSB_bot(Tiempo_msb_bot),
    .LSB_bot(Tiempo_lsb_bot));
  assign controlled_buffer_2_out = maquina_de_estados_se ? Tiempo_msb_bot : 3'bz;  // Controlled_Buffer controlled_buffer_2
  LED LRV (.in(Decodificador_lrv));
  LED LAV (.in(Decodificador_lav));
  LED LVV (.in(Decodificador_lvv));
  LED LRP (.in(Decodificador_lrp));
  LED LVP (.in(Decodificador_lvp));
  assign controlled_buffer_3_out = maquina_de_estados_se ? Tiempo_lsb_top : 4'bz;  // Controlled_Buffer controlled_buffer_3
  _7_Segment_Display u_7_segment_display_1 (
    .g(controlled_buffer_1_out[0]), .f(controlled_buffer_1_out[1]), .a(controlled_buffer_1_out[2]),
    .b(controlled_buffer_1_out[3]), .e(controlled_buffer_2_out[2]), .d(controlled_buffer_2_out[1]),
    .c(controlled_buffer_2_out[0]));  // open: dp
  _7_Segment_Display u_7_segment_display_2 (
    .g(controlled_buffer_3_out[0]), .f(controlled_buffer_3_out[1]), .a(controlled_buffer_3_out[2]),
    .b(controlled_buffer_3_out[3]), .e(controlled_buffer_4_out[2]), .d(controlled_buffer_4_out[1]),
    .c(controlled_buffer_4_out[0]));  // open: dp
  assign controlled_buffer_4_out = maquina_de_estados_se ? Tiempo_lsb_bot : 3'bz;  // Controlled_Buffer controlled_buffer_4

  // Notes on the sheet:
  //   Semáforo Vehicular
  //   Semáforo Peatonal
  //   Pantalla Peatonal
endmodule

module Tiempo (
  input  EN,
  input  CLK,
  input  LOAD,
  input  TS,
  output [5:0] num,
  output ZERO,
  output [3:0] LSB_top,
  output [3:0] MSB_top,
  output [2:0] MSB_bot,
  output [2:0] LSB_bot
);

  wire [5:0] multiplexer_1_out;

  Multiplexer #(.width(6), .enable("false")) multiplexer_1 (
    .in0(6'b101000), .in1(6'b001010), .out(multiplexer_1_out), .sel(TS));
  contador_main main_1 (
    .SET(1'b0), .RESET(1'b0), .M(multiplexer_1_out[5]), .N(multiplexer_1_out[4]), .O(multiplexer_1_out[3]),
    .P(multiplexer_1_out[2]), .Q(multiplexer_1_out[1]), .R(multiplexer_1_out[0]), .LOAD(LOAD), .CLK(CLK),
    .MODE(1'b0), .EN(EN), .num(num), .LSB_top(LSB_top), .MSB_top(MSB_top), .MSB_bot(MSB_bot),
    .LSB_bot(LSB_bot), .ZERO(ZERO));  // open: MAX
  _7_Segment_Display u_7_segment_display_1 (
    .g(MSB_top[0]), .f(MSB_top[1]), .a(MSB_top[2]), .b(MSB_top[3]), .e(MSB_bot[2]), .d(MSB_bot[1]),
    .c(MSB_bot[0]));  // open: dp
  _7_Segment_Display u_7_segment_display_2 (
    .g(LSB_top[0]), .f(LSB_top[1]), .a(LSB_top[2]), .b(LSB_top[3]), .e(LSB_bot[2]), .d(LSB_bot[1]),
    .c(LSB_bot[0]));  // open: dp
endmodule

module Decodificador_de_Salidas (
  input  S1,
  input  S0,
  output LRV,
  output LAV,
  output LVV,
  output LRP,
  output LVP
);

  wire not_1_out, not_2_out;

  not not_1 (not_1_out, S0);
  not not_2 (not_2_out, S1);
  and and_1 (LAV, not_2_out, S0);
  and and_2 (LVV, not_2_out, not_1_out);
  or or_1 (LRP, not_2_out, S0);
  and and_3 (LVP, S1, not_1_out);

  assign LRV = S1;
endmodule

module SP (
  input  CLK,
  input  SP,
  input  RES,
  input  LVP,
  output SP_prime
);

  wire or_1_out;

  S_R_Flip_Flop s_r_ff_1 (.S(1'b0), .clk(CLK), .R(1'b0), .Q(SP_prime), .preset(SP), .reset(or_1_out));  // open: Qn, en
  or or_1 (or_1_out, RES, LVP);

  // Notes on the sheet:
  //   Memoria de Solicitud de Paso
  //   Este circuito "recuerda" que pasó una solicitud de paso hasta que se de paso a los peatones.
endmodule

module Maquina_de_Estados (
  input  CLK,
  input  ZERO,
  input  SP_prime,
  input  RES,
  output S1,
  output S0,
  output SE,
  output LOAD,
  output TS
);

  wire and_1_out, and_2_out, and_3_out, and_4_out, and_5_out, and_6_out, and_7_out, not_1_out, not_2_out,
       or_1_out, or_2_out, Z_q;

  and and_1 (and_1_out, S0, Z_q, ZERO);
  and and_2 (and_2_out, Z_q, ZERO, SP_prime);
  or or_1 (or_1_out, and_2_out, and_3_out);
  and and_3 (and_3_out, S1, Z_q, ZERO);
  and and_4 (and_4_out, Z_q, ZERO);
  not not_1 (not_1_out, Z_q);
  and and_5 (and_5_out, ZERO, SP_prime);
  and and_6 (and_6_out, S0, ZERO);
  and and_7 (and_7_out, S1, ZERO);
  J_K_Flip_Flop X (.J(and_1_out), .clk(CLK), .K(and_1_out), .Q(S1), .reset(RES));  // open: Qn, preset, en
  or or_2 (or_2_out, not_1_out, and_5_out, and_6_out, and_7_out);
  J_K_Flip_Flop Y (.J(or_1_out), .clk(CLK), .K(and_4_out), .Q(S0), .reset(RES));  // open: Qn, preset, en
  J_K_Flip_Flop Z (.J(1'b1), .clk(CLK), .K(or_2_out), .Q(Z_q), .reset(RES));  // open: Qn, preset, en
  not not_2 (not_2_out, S0);
  not not_3 (LOAD, Z_q);
  and and_8 (SE, S1, not_2_out, Z_q);

  assign TS = S0;
endmodule

module ZERO (
  input  CLK,
  input  ZERO,
  input  LOAD,
  input  RES,
  output ZERO_2
);

  wire not_1_out, or_1_out;

  not not_1 (not_1_out, CLK);
  or or_1 (or_1_out, LOAD, RES);
  S_R_Flip_Flop s_r_ff_1 (.S(ZERO), .clk(not_1_out), .R(or_1_out), .Q(ZERO_2));  // open: Qn, preset, reset, en
endmodule
