// Logisim project semaforo.circ as structural Verilog: 5 circuits, main circuit main
module main (
  input  RES
);

  wire CLK_out, DS_lav, DS_lrp, DS_lrv, DS_lvv, ME_load, ME_s0, ME_s1, ME_se, ME_ts,
       modulo_de_tiempos_1_zero, MSP_sp_prime, SP_out;
  wire [2:0] controlled_buffer_2_out, controlled_buffer_4_out, modulo_de_tiempos_1_lsb_bot,
       modulo_de_tiempos_1_msb_bot;
  wire [3:0] controlled_buffer_1_out, controlled_buffer_3_out, modulo_de_tiempos_1_lsb_top,
       modulo_de_tiempos_1_msb_top;

  Clock CLK (.out(CLK_out));
  Button SP (.out(SP_out));
  Solicitud_de_Paso MSP (.SP(SP_out), .CLK(CLK_out), .RES(RES), .LVP(RES), .SP_prime(MSP_sp_prime));
  Maquina_de_Estados ME (
    .CLK(CLK_out), .ZERO(modulo_de_tiempos_1_zero), .SP_prime(MSP_sp_prime), .RES(RES), .S1(ME_s1),
    .S0(ME_s0), .SE(ME_se), .LOAD(ME_load), .TS(ME_ts));
  Decodificador_de_Salidas DS (
    .S1(ME_s1), .S0(ME_s0), .LRV(DS_lrv), .LAV(DS_lav), .LVV(DS_lvv), .LRP(DS_lrp), .LVP(RES));
  Modulo_de_Tiempos modulo_de_tiempos_1 (
    .SET(1'b0), .RESET(RES), .CLK(CLK_out), .LOAD(ME_load), .TS(ME_ts), .EN(1'b1),
    .MSB_top(modulo_de_tiempos_1_msb_top), .LSB_top(modulo_de_tiempos_1_lsb_top),
    .MSB_bot(modulo_de_tiempos_1_msb_bot), .LSB_bot(modulo_de_tiempos_1_lsb_bot),
    .ZERO(modulo_de_tiempos_1_zero));
  LED LRV (.in(DS_lrv));
  LED LAV (.in(DS_lav));
  LED LVV (.in(DS_lvv));
  LED LRP (.in(DS_lrp));
  LED LVP (.in(RES));
  assign controlled_buffer_1_out = ME_se ? modulo_de_tiempos_1_msb_top : 4'bz;  // Controlled_Buffer controlled_buffer_1
  _7_Segment_Display u_7_segment_display_1 (
    .g(controlled_buffer_1_out[0]), .f(controlled_buffer_1_out[1]), .a(controlled_buffer_1_out[2]),
    .b(controlled_buffer_1_out[3]), .e(controlled_buffer_2_out[2]), .d(controlled_buffer_2_out[2]),
    .c(controlled_buffer_2_out[0]));  // open: dp
  assign {{2{controlled_buffer_2_out[2]}}, controlled_buffer_2_out[0]} = ME_se ? modulo_de_tiempos_1_msb_bot : 3'bz;  // Controlled_Buffer controlled_buffer_2
  assign controlled_buffer_3_out = ME_se ? modulo_de_tiempos_1_lsb_top : 4'bz;  // Controlled_Buffer controlled_buffer_3
  _7_Segment_Display u_7_segment_display_2 (
    .g(controlled_buffer_3_out[0]), .f(controlled_buffer_3_out[1]), .a(controlled_buffer_3_out[2]),
    .b(controlled_buffer_3_out[3]), .e(controlled_buffer_4_out[2]), .d(controlled_buffer_4_out[1]),
    .c(controlled_buffer_4_out[0]));  // open: dp
  assign controlled_buffer_4_out = ME_se ? modulo_de_tiempos_1_lsb_bot : 3'bz;  // Controlled_Buffer controlled_buffer_4
endmodule

module Maquina_de_Estados (
  input  CLK,
  input  ZERO,
  input  SP_prime,
  input  RES,
  output S1,
  output S0,
  output SE,
  output LOAD,
  output TS
);

  wire and_1_out, and_2_out, and_3_out, and_4_out, not_1_out, not_2_out, or_1_out, or_2_out, Z_q;

  and and_1 (and_1_out, S0, Z_q, ZERO);
  and and_2 (and_2_out, Z_q, ZERO, SP_prime);
  or or_1 (or_1_out, and_2_out, and_3_out);
  and and_3 (and_3_out, S1, Z_q, ZERO);
  and and_4 (and_4_out, Z_q, ZERO);
  not not_1 (not_1_out, Z_q);
  or or_2 (or_2_out, not_1_out, ZERO);
  J_K_Flip_Flop X (.J(and_1_out), .clk(CLK), .K(and_1_out), .Q(S1), .preset(1'b0), .en(1'b1), .reset(RES));  // open: Qn
  J_K_Flip_Flop Y (.J(or_1_out), .clk(CLK), .K(and_4_out), .Q(S0), .preset(1'b0), .en(1'b1), .reset(RES));  // open: Qn
  J_K_Flip_Flop Z (.J(1'b1), .clk(CLK), .K(or_2_out), .Q(Z_q), .preset(1'b0), .en(1'b1), .reset(RES));  // open: Qn
  not not_2 (not_2_out, S0);
  not not_3 (LOAD, Z_q);
  and and_5 (SE, S1, not_2_out, Z_q);

  assign TS = S0;
endmodule

module Decodificador_de_Salidas (
  input  S1,
  input  S0,
  output LRV,
  output LAV,
  output LVV,
  output LRP,
  output LVP
);

  wire not_1_out, not_2_out;

  not not_1 (not_1_out, S0);
  not not_2 (not_2_out, S1);
  and and_1 (LAV, not_2_out, S0);
  and and_2 (LVV, not_2_out, not_1_out);
  or or_1 (LRP, not_2_out, S0);
  and and_3 (LVP, S1, not_1_out);

  assign LRV = S1;
endmodule

module Modulo_de_Tiempos (
  input  CLK,
  input  EN,
  input  SET,
  input  RESET,
  input  LOAD,
  input  TS,
  output [3:0] MSB_top,
  output [3:0] LSB_top,
  output [2:0] MSB_bot,
  output [2:0] LSB_bot,
  output ZERO
);

  wire [5:0] estado_1_out_6, multiplexer_1_out, multiplexer_2_out, multiplexer_3_out, previo_1_out,
       siguiente_1_out;

  Multiplexer #(.width(6), .enable("false")) multiplexer_1 (
    .in0(previo_1_out), .in1(siguiente_1_out), .out(multiplexer_1_out), .sel(1'b0));
  Multiplexer #(.width(6), .enable("false")) multiplexer_2 (
    .in0(multiplexer_1_out), .in1(multiplexer_3_out), .out(multiplexer_2_out), .sel(LOAD));
  Multiplexer #(.width(6), .enable("false")) multiplexer_3 (
    .in0(6'b101000), .in1(6'b001010), .out(multiplexer_3_out), .sel(TS));
  estado estado_1 (.CLK(CLK), .D(multiplexer_2_out), .S(SET), .EN(EN), .R(RESET), .out_6(estado_1_out_6));
  previo previo_1 (.IN(estado_1_out_6), .OUT(previo_1_out));
  siguiente siguiente_1 (.IN(estado_1_out_6), .OUT(siguiente_1_out));
  _6bit2bcd_main main_1 (
    .in_1(estado_1_out_6), .MSB_top(MSB_top), .LSB_top(LSB_top), .MSB_bot(MSB_bot), .LSB_bot(LSB_bot));
  zero_max zero_max_1 (.in_1(estado_1_out_6), .ZERO(ZERO));  // open: MAX
  _7_Segment_Display u_7_segment_display_1 (
    .g(MSB_top[0]), .f(MSB_top[1]), .a(MSB_top[2]), .b(MSB_top[3]), .e(MSB_bot[2]), .d(MSB_bot[1]),
    .c(MSB_bot[0]));  // open: dp
  _7_Segment_Display u_7_segment_display_2 (
    .g(LSB_top[0]), .f(LSB_top[1]), .a(LSB_top[2]), .b(LSB_top[3]), .e(LSB_bot[2]), .d(LSB_bot[1]),
    .c(LSB_bot[0]));  // open: dp
endmodule

module Solicitud_de_Paso (
  input  SP,
  input  CLK,
  input  RES,
  input  LVP,
  output SP_prime
);

  wire or_1_out;

  S_R_Flip_Flop s_r_ff_1 (.S(1'b0), .clk(CLK), .R(1'b0), .Q(SP_prime), .preset(SP), .reset(or_1_out));  // open: Qn, en
  or or_1 (or_1_out, RES, LVP);
endmodule
